// Logisim project first.circ as structural Verilog: 1 circuit, main circuit main
// 1
module main (
  output out_1,
  output out_2,
  output out_3,
  output out_4,
  output out_5,
  output out_6,
  output out_7,
  output out_8,
  output out_9
);

  wire _1_out, _2_out, _3_out, and_2_out, and_3_out, and_5_out, and_6_out, and_7_out, and_8_out, not_1_out,
       not_2_out;

  Button _1 (.out(_1_out));
  Button _2 (.out(_2_out));
  Button _3 (.out(_3_out));
  not not_1 (not_1_out, _1_out);
  not not_2 (not_2_out, _2_out);
  not not_3 (out_3, _3_out);
  and and_1 (out_1, _1_out, _2_out, _3_out);
  and and_2 (and_2_out, _1_out, not_2_out, _3_out);
  or or_1 (out_6, and_2_out, and_3_out);
  and and_3 (and_3_out, _1_out, _2_out, out_3);
  and and_4 (out_5, _1_out, out_3);
  and and_5 (and_5_out, _1_out, not_2_out, _3_out);
  and and_6 (and_6_out, _2_out, not_2_out);
  or or_2 (out_7, and_5_out, and_6_out);
  and and_7 (and_7_out, not_1_out, _2_out);
  and and_8 (and_8_out, _2_out, out_3);
  or or_3 (out_8, and_2_out, and_7_out, and_8_out);
  or or_4 (out_9, _3_out, _2_out);

  assign out_2 = 1'b0;
  assign out_4 = 1'b1;
endmodule
