// Logisim project second.circ as structural Verilog: 1 circuit, main circuit main
module main (
);

  wire decoder_1_out0, decoder_1_out1, decoder_1_out2, decoder_1_out3, decoder_1_out4, decoder_1_out5,
       decoder_1_out6;

  Decoder #(.select(3)) decoder_1 (
    .out0(decoder_1_out0), .out1(decoder_1_out1), .out2(decoder_1_out2), .out3(decoder_1_out3),
    .out4(decoder_1_out4), .out5(decoder_1_out5), .out6(decoder_1_out6), .out7(decoder_1_out6));  // open: sel, en
  // OR_Gate _0 has open pins: in0=decoder_1_out0, in1=decoder_1_out1, in2=decoder_1_out2, in3=decoder_1_out3, in4=decoder_1_out4, in5=decoder_1_out5, in6=decoder_1_out6, out=open
  // OR_Gate _1 has open pins: in0=decoder_1_out2, in1=decoder_1_out3, in2=decoder_1_out6, out=open
  // OR_Gate _2 has open pins: in0=decoder_1_out3, in1=decoder_1_out4, in2=decoder_1_out6, in3=decoder_1_out6, out=open
  // OR_Gate _3 has open pins: in0=decoder_1_out0, in1=decoder_1_out1, in2=decoder_1_out2, in3=decoder_1_out3, in4=decoder_1_out4, in5=decoder_1_out6, out=open
  // OR_Gate _4 has open pins: in0=decoder_1_out4, in1=decoder_1_out5, in2=decoder_1_out6, out=open
  // OR_Gate _5 has open pins: in0=decoder_1_out5, in1=decoder_1_out4, in2=decoder_1_out3, in3=decoder_1_out2, in4=decoder_1_out1, in5=decoder_1_out0, out=open
  // OR_Gate _6 has open pins: in0=decoder_1_out6, in1=decoder_1_out6, out=open
endmodule
